# Fritzing sketch jellyfish (saved by Fritzing 0.9.2b)
breadboards: 1

parts:
  LED1 = smd LED [color="Blue (430nm)" package="1206 [SMD]"]
  LED3 = smd LED [color="Blue (430nm)" package="1206 [SMD]"]
  LED5 = smd LED [color="Blue (430nm)" package="1206 [SMD]"]
  LED6 = smd LED [color="Blue (430nm)" package="1206 [SMD]"]
  LED7 = smd LED [color="Blue (430nm)" package="1206 [SMD]"]
  LED2 = smd LED [color="Blue (430nm)" package="1206 [SMD]"]
  R1 = Resistor [tolerance=±5% resistance=150 package="0603 [SMD]"]
  R2 = Resistor [tolerance=±5% resistance=150 package="0603 [SMD]"]
  R3 = Resistor [tolerance=±5% resistance=120 package="1206 [SMD]"]
  R4 = Resistor [tolerance=±5% resistance=750 package="0603 [SMD]"]
  Q1 = TRANSISTOR_NPN [package=to-92]
  R5 = Resistor [tolerance=±5% resistance=0 package="1206 [SMD]"]
  U1 = Voltage Regulator [package=to220-adj]

nets:
  N1: LED1.cathode, LED2.anode
  N2: LED1.anode, R1.Pin_1
  N3: LED3.cathode, LED7.cathode, Q1.C
  N4: LED3.anode, LED2.cathode
  N5: LED5.cathode, LED6.anode
  N6: LED5.anode, R2.Pin_1
  N7: LED6.cathode, LED7.anode
  N8: R1.Pin_0, R2.Pin_0, R3.Pin_1, U1.OUT
  N9: R3.Pin_0, R4.Pin_1, U1.ADJ
  GND: R4.Pin_0, Q1.E
  N10: Q1.B, R5.Pin_0

notes:
  Each leg the total voltage drop across all three LEDs is 10.8V.
  With 75ohm If Vcc is13.7V, then the current through each leg is 19.3ma
  s
